// Logisim project ALU_A1_G1_v2_combined.circ as structural Verilog: 1 circuit, main circuit main
module main (
  input  Vcc,
  input  A4,
  input  A3,
  input  A2,
  input  A1,
  input  B4,
  input  B3,
  input  B2,
  input  B1,
  input  GND,
  output s4,
  output s3,
  output s2,
  output s1
);

  wire input_preprocessor_1_p1, input_preprocessor_1_p2, input_preprocessor_1_p3, input_preprocessor_1_p4,
       input_preprocessor_1_p5, input_preprocessor_1_p6, input_preprocessor_1_p7, input_preprocessor_1_p8,
       input_preprocessor_1_p9;

  // input_preprocessor input_preprocessor_1: pin names not known; wires that end beside it: input_preprocessor_1_p1, input_preprocessor_1_p2, input_preprocessor_1_p3, input_preprocessor_1_p4, input_preprocessor_1_p5, input_preprocessor_1_p6, input_preprocessor_1_p7, input_preprocessor_1_p8, input_preprocessor_1_p9, input_preprocessor_1_p2, input_preprocessor_1_p3, input_preprocessor_1_p4, input_preprocessor_1_p5, input_preprocessor_1_p6, input_preprocessor_1_p7, input_preprocessor_1_p8, input_preprocessor_1_p9
  // _7483 7483_1: pin names not known; wires that end beside it: A4, s3, A3, B3, Vcc, s2, B2, A2, B4, s4, input_preprocessor_1_p1, GND, B1, A1, s1
endmodule
