// Logisim project ALU_A1_G1_v2_upto_control_preprocessor.circ as structural Verilog
module main (
  input  CS2,
  input  cs1,
  input  cs0,
  input  a3,
  input  B3,
  input  A2,
  input  B2,
  input  A1,
  input  B1,
  input  A0,
  input  B0,
  output Sx0,
  output Sx1,
  output Sy0
);

  wire n7408_1_p1, n7408_1_p4;

  // _7408 7408_1: pin names not known; wires that end beside it: n7408_1_p1, cs0, Sx0, n7408_1_p4, CS2, Sx1, 1'b0, 1'b1
  // _7404 7404_1: pin names not known; wires that end beside it: CS2, cs1, n7408_1_p1, a3, 1'b0, 1'b1, A0, A1, A2
  // _7408 7408_2: pin names not known; wires that end beside it: a3, B3, A2, B2, 1'b0, 1'b1, A0, B0, A1, B1
  // _7432 7432_1: pin names not known; wires that end beside it: cs1, cs0, n7408_1_p4, Sx0, CS2, Sy0, 1'b0, 1'b1
  // _7486 7486_1: pin names not known; wires that end beside it: a3, B3, A2, B2, 1'b0, 1'b1, A0, B0, A1, B1
  // _74153 74153_1: pin names not known; wires that end beside it: A0, A2
  // _74153 74153_2: pin names not known
endmodule

module control_preprocessor (
  input  cs2,
  input  cs1,
  input  cs0,
  output Sx0,
  output Sx1,
  output Sy0,
  output Cin
);

  wire n7408_1_p1, n7408_1_p4, n7408_1_p9, n7408_1_p11, n7408_1_p12, n7408_1_p14;

  // _7408 7408_1: pin names not known; wires that end beside it: n7408_1_p1, cs0, Sx0, n7408_1_p4, cs2, Sx1, 1'b0, 1'b1, n7408_1_p9, cs0, n7408_1_p11, n7408_1_p12, cs2, n7408_1_p14
  // _7404 7404_1: pin names not known; wires that end beside it: cs2, n7408_1_p9, cs1, n7408_1_p1, n7408_1_p4, n7408_1_p12, 1'b0, 1'b1
  // _7432 7432_1: pin names not known; wires that end beside it: cs1, cs0, n7408_1_p4, Sx0, cs2, Sy0, 1'b0, 1'b1, n7408_1_p14, n7408_1_p11, Cin
endmodule

module input_preprocessor (
  input  cs2,
  input  cs1,
  input  cs0,
  input  A3,
  input  B3,
  input  A2,
  input  B2,
  input  A1,
  input  B1,
  input  A0,
  input  B0
);

  control_preprocessor Control_Preprocessor (.cs2(cs2), .cs1(cs1), .cs0(cs0));  // open: Sx0, Sx1, Sy0, Cin
  // _7408 7408_1: pin names not known; wires that end beside it: A3, B3, A2, B2, 1'b0, 1'b1, A0, B0, A1, B1
  // _7486 7486_1: pin names not known; wires that end beside it: A3, B3, A2, B2, 1'b0, 1'b1, A0, B0, A1, B1
endmodule
