// Logisim project ALU_A1_G1_v2_upto_flag.circ as structural Verilog
module main (
  input  CS2,
  input  cs1,
  input  cs0,
  input  a3,
  input  B3,
  input  A2,
  input  B2,
  input  A1,
  input  B1,
  input  A0,
  input  B0,
  output Sx0,
  output Sx1,
  output Sy0
);

  wire n7408_1_p1, n7408_1_p4;

  // _7408 7408_1: pin names not known; wires that end beside it: n7408_1_p1, cs0, Sx0, n7408_1_p4, CS2, Sx1, 1'b0, 1'b1
  // _7404 7404_1: pin names not known; wires that end beside it: CS2, cs1, n7408_1_p1, a3, 1'b0, 1'b1, A0, A1, A2
  // _7408 7408_2: pin names not known; wires that end beside it: a3, B3, A2, B2, 1'b0, 1'b1, A0, B0, A1, B1
  // _7432 7432_1: pin names not known; wires that end beside it: cs1, cs0, n7408_1_p4, Sx0, CS2, Sy0, 1'b0, 1'b1
  // _7486 7486_1: pin names not known; wires that end beside it: a3, B3, A2, B2, 1'b0, 1'b1, A0, B0, A1, B1
  // _74153 74153_1: pin names not known; wires that end beside it: A0, A2
  // _74153 74153_2: pin names not known
endmodule

module control_preprocessor (
  input  cs2,
  input  cs1,
  input  cs0,
  output Sx0,
  output Sx1,
  output Sy0,
  output Cin
);

  wire n7408_1_p1, n7408_1_p4, n7408_1_p9, n7408_1_p11, n7408_1_p12, n7408_1_p14;

  // _7408 7408_1: pin names not known; wires that end beside it: n7408_1_p1, cs0, Sx0, n7408_1_p4, cs2, Sx1, 1'b0, 1'b1, n7408_1_p9, cs0, n7408_1_p11, n7408_1_p12, cs2, n7408_1_p14
  // _7404 7404_1: pin names not known; wires that end beside it: cs2, n7408_1_p9, cs1, n7408_1_p1, n7408_1_p4, n7408_1_p12, 1'b0, 1'b1
  // _7432 7432_1: pin names not known; wires that end beside it: cs1, cs0, n7408_1_p4, Sx0, cs2, Sy0, 1'b0, 1'b1, n7408_1_p14, n7408_1_p11, Cin
endmodule

// Input Preprocessor
module input_preprocessor (
  input  cs2,
  input  cs1,
  input  cs0,
  input  A3,
  input  B3,
  input  A2,
  input  B2,
  input  A1,
  input  B1,
  input  A0,
  input  B0,
  output cin,
  output x3,
  output x2,
  output x1,
  output x0,
  output y3,
  output y2,
  output y1,
  output y0
);

  wire Control_Preprocessor_sx0, Control_Preprocessor_sx1, Control_Preprocessor_sy0, n7404_1_p2, n7404_1_p4,
       n7404_1_p6, n7404_1_p10, n7408_1_p3, n7408_1_p6, n7408_1_p11, n7408_1_p14, n7486_1_p3, n7486_1_p6,
       n7486_1_p11, n7486_1_p14;

  control_preprocessor Control_Preprocessor (
    .cs2(cs2), .cs1(cs1), .cs0(cs0), .Sx0(Control_Preprocessor_sx0), .Sx1(Control_Preprocessor_sx1),
    .Sy0(Control_Preprocessor_sy0), .Cin(cin));
  // _7408 7408_1: pin names not known; wires that end beside it: A3, B3, n7408_1_p3, A2, B2, n7408_1_p6, 1'b0, 1'b1, A0, B0, n7408_1_p11, A1, B1, n7408_1_p14
  // _7404 7404_1: pin names not known; wires that end beside it: A3, n7404_1_p2, A2, n7404_1_p4, A1, n7404_1_p6, 1'b0, 1'b1, A0, n7404_1_p10
  // _7486 7486_1: pin names not known; wires that end beside it: A3, B3, n7486_1_p3, A2, B2, n7486_1_p6, 1'b0, 1'b1, A0, B0, n7486_1_p11, A1, B1, n7486_1_p14
  // _74153 74153_1: pin names not known; wires that end beside it: 1'b0, Control_Preprocessor_sx1, n7408_1_p3, n7486_1_p3, n7404_1_p2, A3, x3, 1'b0, 1'b1, 1'b0, Control_Preprocessor_sx0, n7408_1_p6, n7486_1_p6, n7404_1_p4, A2, x2, x3
  // _74153 74153_2: pin names not known; wires that end beside it: 1'b0, Control_Preprocessor_sx1, n7408_1_p14, n7486_1_p14, n7404_1_p6, A1, x1, 1'b0, 1'b1, 1'b0, Control_Preprocessor_sx0, n7408_1_p11, n7486_1_p11, n7404_1_p10, A0, x0
  // _74157 74157_1: pin names not known; wires that end beside it: Control_Preprocessor_sy0, B3, 1'b0, y3, B2, 1'b0, y2, 1'b0, 1'b1, 1'b0, B0, 1'b0, y0, B1, 1'b0, y1
endmodule

module full_adder_and_overflow (
  input  cs2,
  input  cs1,
  input  cs0,
  input  A3,
  input  A2,
  input  A1,
  input  A0,
  input  B3,
  input  B2,
  input  B1,
  input  B0,
  output Cout,
  output S3,
  output S2,
  output S1,
  output S0,
  output S,
  output C,
  output Z,
  output V
);

  wire input_preprocessor_1_cin, input_preprocessor_1_x0, input_preprocessor_1_x1, input_preprocessor_1_x2,
       input_preprocessor_1_x3, input_preprocessor_1_y0, input_preprocessor_1_y1, input_preprocessor_1_y2,
       input_preprocessor_1_y3, n7432_1_p3, n7432_1_p6, n7432_1_p10, n7486_1_p6, n7486_1_p10;

  input_preprocessor input_preprocessor_1 (
    .cs2(cs2), .cs1(cs1), .cs0(cs0), .A3(A3), .B3(B3), .A2(A2), .B2(B2), .A1(A1), .B1(B1), .A0(A0), .B0(B0),
    .cin(input_preprocessor_1_cin), .x3(input_preprocessor_1_x3), .x2(input_preprocessor_1_x2),
    .x1(input_preprocessor_1_x1), .x0(input_preprocessor_1_x0), .y3(input_preprocessor_1_y3),
    .y2(input_preprocessor_1_y2), .y1(input_preprocessor_1_y1), .y0(input_preprocessor_1_y0));
  _7483__corrected u_7483_corrected_1 (
    ._1__A4(input_preprocessor_1_x3), ._2__S3(S2), ._3__A3(input_preprocessor_1_x2),
    ._4__B3(input_preprocessor_1_y2), ._5__Vcc(1'b1), ._6__S2(S1), ._7__B2(input_preprocessor_1_y1),
    ._8__A2(input_preprocessor_1_x1), ._16__B4(input_preprocessor_1_y3), ._15__S4(S), ._14__Cout(C),
    ._13__Cin(input_preprocessor_1_cin), ._12__GND(1'b0), ._11__B1(input_preprocessor_1_y0),
    ._10__A1(input_preprocessor_1_x0), ._9__S1(S0));
  // _7432 7432_1: pin names not known; wires that end beside it: S, S2, n7432_1_p3, n7432_1_p3, S1, n7432_1_p6, 1'b1, n7432_1_p6, S0, n7432_1_p10
  // _7486 7486_1: pin names not known; wires that end beside it: 1'b1, n7432_1_p10, Z, input_preprocessor_1_x3, input_preprocessor_1_y3, n7486_1_p6, 1'b0, 1'b1, C, n7486_1_p10, V, S, n7486_1_p6, n7486_1_p10

  assign Cout = C;
  assign S3 = S;
endmodule

// 7483
module _7483__corrected (
  input  _1__A4,
  input  _16__B4,
  input  _3__A3,
  input  _4__B3,
  input  _13__Cin,
  input  _5__Vcc,
  input  _12__GND,
  input  _11__B1,
  input  _7__B2,
  input  _10__A1,
  input  _8__A2,
  output _2__S3,
  output _15__S4,
  output _14__Cout,
  output _6__S2,
  output _9__S1
);

  wire and_1_out, and_2_out, and_3_out, and_4_out, and_5_out, and_6_out, and_7_out, and_8_out, and_9_out,
       and_10_out, and_11_out, and_12_out, and_13_out, and_14_out, nand_1_out, nand_2_out, nand_3_out,
       nand_4_out, nor_1_out, nor_2_out, nor_3_out, nor_4_out, nor_6_out, nor_7_out, nor_8_out, not_1_out,
       not_2_out, not_3_out, not_4_out, not_5_out, not_6_out;

  nand nand_1 (nand_1_out, _16__B4, _1__A4);
  nor nor_1 (nor_1_out, _16__B4, _1__A4);
  nand nand_2 (nand_2_out, _4__B3, _3__A3);
  nor nor_2 (nor_2_out, _4__B3, _3__A3);
  nand nand_3 (nand_3_out, _7__B2, _8__A2);
  nor nor_3 (nor_3_out, _7__B2, _8__A2);
  nand nand_4 (nand_4_out, _11__B1, _10__A1);
  nor nor_4 (nor_4_out, _11__B1, _10__A1);
  and and_1 (and_1_out, nor_2_out, nand_1_out);
  and and_2 (and_2_out, nor_3_out, nand_1_out, nand_2_out);
  and and_3 (and_3_out, nor_4_out, nand_1_out, nand_2_out, nand_3_out);
  and and_4 (and_4_out, nand_1_out, nand_2_out, nand_3_out, nand_4_out, not_2_out);
  not not_1 (not_1_out, nor_1_out);
  and and_5 (and_5_out, nor_3_out, nand_2_out);
  and and_6 (and_6_out, nor_4_out, nand_2_out, nand_3_out);
  and and_7 (and_7_out, nand_2_out, nand_3_out, nand_4_out, not_2_out);
  not not_2 (not_2_out, _13__Cin);
  not not_3 (not_3_out, nor_2_out);
  and and_8 (and_8_out, nor_4_out, nand_3_out);
  and and_9 (and_9_out, nand_3_out, nand_4_out, not_2_out);
  not not_4 (not_4_out, nor_3_out);
  and and_10 (and_10_out, nand_4_out, not_2_out);
  not not_5 (not_5_out, nor_4_out);
  not not_6 (not_6_out, not_2_out);
  nor nor_5 (_14__Cout, nor_1_out, and_1_out, and_2_out, and_3_out, and_4_out);
  and and_11 (and_11_out, nand_1_out, not_1_out);
  and and_12 (and_12_out, nand_2_out, not_3_out);
  and and_13 (and_13_out, nand_3_out, not_4_out);
  and and_14 (and_14_out, nand_4_out, not_5_out);
  xor xor_1 (_15__S4, and_11_out, nor_6_out);
  nor nor_6 (nor_6_out, nor_2_out, and_5_out, and_6_out, and_7_out);
  xor xor_2 (_2__S3, and_12_out, nor_7_out);
  nor nor_7 (nor_7_out, nor_3_out, and_8_out, and_9_out);
  xor xor_3 (_6__S2, and_13_out, nor_8_out);
  nor nor_8 (nor_8_out, nor_4_out, and_10_out);
  xor xor_4 (_9__S1, and_14_out, not_6_out);

  // Notes on the sheet:
  //   7483: 4-bit full adder
endmodule
