// Logisim project Adder.circ as structural Verilog: 1 circuit, main circuit main
module main (
  input  Vcc,
  input  A4,
  input  A3,
  input  A2,
  input  A1,
  input  Cin,
  input  B4,
  input  B3,
  input  B2,
  input  B1,
  input  GND,
  output s4,
  output s3,
  output s2,
  output s1
);

  // _7483 7483_1: pin names not known; wires that end beside it: A4, s3, A3, B3, Vcc, s2, B2, A2, B4, s4, Cin, GND, B1, A1, s1
endmodule
