// Logisim project Utility.circ as structural Verilog: 3 circuits, main circuit main
module main (
);

  Input_Validator input_validator_1 ();  // open: Fraction_1, Exponent_1, Fraction_2, EXponent_2, Denormalized_Input_1, Denormalized_Input_2, NaN_Input_1, NaN_Input_2, Valid_Fraction_1, Valid_Fraction_2
endmodule

module Single_Input_Checker (
  input  [31:0] Fraction,
  input  [10:0] Exponent,
  output Check_Fraction_Contains_1,
  output Check_Exponent_Contains_1,
  output Check_Exponent_All_1,
  output [31:0] Valid_Fraction
);

  wire [31:0] shifter_1_out;

  Shifter #(.width(32)) shifter_1 (.in(Fraction), .\dist (5'b00010), .out(shifter_1_out));
  Priority_Encoder_32x5 priority_encoder_32x5_1 (
    .in_1(shifter_1_out), .Valid_Bit(Check_Fraction_Contains_1));  // open: A4, A3, A2, A1, A0
  Priority_Encoder_12x4 priority_encoder_12x4_1 (
    .in_1({1'b0, Exponent}), .Valid_Bit(Check_Exponent_Contains_1));  // open: A3, A2, A1, A0
  ALU_12_bit alu_12_bit_1 (
    .Input_1({12{1'b1}}), .Input_2({1'b1, Exponent}), .Control(2'b11), .Zero_Flag(Check_Exponent_All_1));  // open: Output, Carry_Out, Sign_Flag
  MUX_32_bit mux_32_bit_1 (
    .X({32{1'b0}}), .Y(Fraction), .Selection(Check_Exponent_Contains_1), .Output(Valid_Fraction));
endmodule

// INP_Validator
module Input_Validator (
  input  [31:0] Fraction_1,
  input  [10:0] Exponent_1,
  input  [31:0] Fraction_2,
  input  [10:0] EXponent_2,
  output Denormalized_Input_1,
  output Denormalized_Input_2,
  output NaN_Input_1,
  output NaN_Input_2,
  output [31:0] Valid_Fraction_1,
  output [31:0] Valid_Fraction_2
);

  wire n7404_1_p2, n7404_1_p4, single_input_checker_1_check_exponent_all_1,
       single_input_checker_1_check_exponent_contains_1, single_input_checker_1_check_fraction_contains_1,
       single_input_checker_2_check_exponent_all_1, single_input_checker_2_check_exponent_contains_1,
       single_input_checker_2_check_fraction_contains_1;

  Single_Input_Checker single_input_checker_1 (
    .Fraction(Fraction_1), .Exponent(Exponent_1),
    .Check_Fraction_Contains_1(single_input_checker_1_check_fraction_contains_1),
    .Check_Exponent_Contains_1(single_input_checker_1_check_exponent_contains_1),
    .Check_Exponent_All_1(single_input_checker_1_check_exponent_all_1), .Valid_Fraction(Valid_Fraction_1));
  Single_Input_Checker single_input_checker_2 (
    .Fraction(Fraction_2), .Exponent(EXponent_2),
    .Check_Fraction_Contains_1(single_input_checker_2_check_fraction_contains_1),
    .Check_Exponent_Contains_1(single_input_checker_2_check_exponent_contains_1),
    .Check_Exponent_All_1(single_input_checker_2_check_exponent_all_1), .Valid_Fraction(Valid_Fraction_2));
  // _7404 7404_1: pin names not known; wires that end beside it: single_input_checker_1_check_exponent_contains_1, n7404_1_p2, single_input_checker_2_check_exponent_contains_1, n7404_1_p4
  // _7408 7408_1: pin names not known; wires that end beside it: n7404_1_p2, single_input_checker_1_check_fraction_contains_1, Denormalized_Input_1, n7404_1_p4, single_input_checker_2_check_fraction_contains_1, Denormalized_Input_2, single_input_checker_1_check_exponent_all_1, single_input_checker_1_check_fraction_contains_1, NaN_Input_1, single_input_checker_2_check_exponent_all_1, single_input_checker_2_check_fraction_contains_1, NaN_Input_2
endmodule
