// Logisim project Circuit_Tester.circ as structural Verilog: 2 circuits, main circuit Circuit_Tester_Using_RAM_16_bit
module Circuit_Tester_Using_RAM_16_bit (
  output [31:0] Out,
  output [31:0] out_2
);

  wire Clock_out, ram_3_data;
  wire [15:0] Counter_q;
  wire [31:0] ram_1_data, ram_2_data;

  Counter #(.width(16), .max('hffff), .ongoal("stay")) Counter (
    .load(1'b0), .D({16{1'b0}}), .count(1'b1), .Q(Counter_q), .clk(Clock_out), .clr(1'b0));  // open: carry
  Clock Clock (.out(Clock_out));
  RAM #(.addrWidth(16), .dataWidth(32), .bus("asynch")) ram_1 (
    .addr(Counter_q), .data(ram_1_data), .sel(1'b1), .ld(1'b1), .clr(1'b0));
  RAM #(.addrWidth(16), .dataWidth(32), .bus("asynch")) ram_2 (
    .addr(Counter_q), .data(ram_2_data), .sel(1'b1), .ld(1'b1), .clr(1'b0));
  FPA fpa_1 (
    .Input_2(ram_2_data), .Input_1(ram_1_data), .Output(Out));  // open: Denormalized_Input_1, Denormalized_Input_2, NaN_Input_1, NaN_Input_2, Overflow, Underflow
  RAM #(.addrWidth(16), .dataWidth(1), .bus("asynch")) ram_3 (
    .addr(Counter_q), .data(ram_3_data), .sel(1'b1), .ld(1'b0), .clr(1'b0));
  Comparator #(.width(32)) comparator_1 (.a(out_2), .b(Out), .eq(ram_3_data));  // open: gt, lt
  LED led_1 (.in(ram_3_data));
  RAM #(.addrWidth(16), .dataWidth(32), .bus("asynch")) ram_4 (
    .addr(Counter_q), .data(out_2), .sel(1'b1), .ld(1'b1), .clr(1'b0));
endmodule

module Circuit_Tester_Using_RAM_8_bit (
  output [31:0] Out,
  output [31:0] out_2
);

  wire Clock_out, ram_3_data;
  wire [7:0] Counter_q;
  wire [31:0] ram_1_data, ram_2_data;

  Counter #(.ongoal("stay")) Counter (
    .load(1'b0), .D({8{1'b0}}), .count(1'b1), .Q(Counter_q), .clk(Clock_out), .clr(1'b0));  // open: carry
  Clock Clock (.out(Clock_out));
  RAM #(.dataWidth(32), .bus("asynch")) ram_1 (.addr(Counter_q), .data(ram_1_data), .sel(1'b1), .ld(1'b1), .clr(1'b0));
  RAM #(.dataWidth(32), .bus("asynch")) ram_2 (.addr(Counter_q), .data(ram_2_data), .sel(1'b1), .ld(1'b1), .clr(1'b0));
  FPA fpa_1 (
    .Input_2(ram_2_data), .Input_1(ram_1_data), .Output(Out));  // open: Denormalized_Input_1, Denormalized_Input_2, NaN_Input_1, NaN_Input_2, Overflow, Underflow
  RAM #(.dataWidth(1), .bus("asynch")) ram_3 (.addr(Counter_q), .data(ram_3_data), .sel(1'b1), .ld(1'b0), .clr(1'b0));
  Comparator #(.width(32)) comparator_1 (.a(out_2), .b(Out), .eq(ram_3_data));  // open: gt, lt
  LED led_1 (.in(ram_3_data));
  RAM #(.dataWidth(32), .bus("asynch")) ram_4 (.addr(Counter_q), .data(out_2), .sel(1'b1), .ld(1'b1), .clr(1'b0));
endmodule
