// Logisim project Floating_Point_Adder.circ as structural Verilog: 2 circuits, main circuit FPA
module FPA (
  input  [31:0] Input_2,
  input  [31:0] Input_1,
  output Denormalized_Input_1,
  output Denormalized_Input_2,
  output NaN_Input_1,
  output NaN_Input_2,
  output Overflow,
  output Underflow,
  output [31:0] Output
);

  wire n7486_1_p3, normalizer_1_overflow, normalizer_1_underflow, normalizer_2_overflow,
       normalizer_2_underflow;
  wire [4:0] Comparator_difference;
  wire [10:0] Comparator_common_exponent, normalizer_1_normalized_exponent;
  wire [11:0] shifter_2_out;
  wire [31:0] Adder_Subtractor_result, Comparator_largerfraction, Comparator_smallerfraction,
       input_validator_1_valid_fraction_1, input_validator_1_valid_fraction_2,
       normalizer_1_normalized_fraction, normalizer_2_normalized_fraction, Rounder_output, shifter_1_out;

  Input_Validator input_validator_1 (
    .Fraction_1({2'b01, Input_1[19:0], {10{1'b0}}}), .Exponent_1(Input_1[30:20]),
    .Fraction_2({2'b01, Input_2[19:0], {10{1'b0}}}), .EXponent_2(Input_2[30:20]),
    .Denormalized_Input_1(Denormalized_Input_1), .Denormalized_Input_2(Denormalized_Input_2),
    .NaN_Input_1(NaN_Input_1), .NaN_Input_2(NaN_Input_2),
    .Valid_Fraction_1(input_validator_1_valid_fraction_1),
    .Valid_Fraction_2(input_validator_1_valid_fraction_2));
  Comparator_With_Smaller_Fraction Comparator (
    .X_fraction(input_validator_1_valid_fraction_1), .Y_fraction(input_validator_1_valid_fraction_2),
    .X(Input_1[30:20]), .Y(Input_2[30:20]), .LargerFraction(Comparator_largerfraction),
    .SmallerFraction(Comparator_smallerfraction), .Common_Exponent(Comparator_common_exponent),
    .Difference(Comparator_difference));  // open: X_Y
  Shifter #(.width(32), .shift("lr")) shifter_1 (
    .in(Comparator_smallerfraction), .\dist (Comparator_difference), .out(shifter_1_out));
  Adder_Subtractor Adder_Subtractor (
    .X(Comparator_largerfraction), .Y(shifter_1_out), .SignBit1(Input_1[31]), .SignBit2(Input_2[31]),
    .Sign_of_Result(Output[31]), .Result(Adder_Subtractor_result));
  Normalizer normalizer_1 (
    .Fraction(Adder_Subtractor_result), .Exponent(Comparator_common_exponent),
    .Normalized_Fraction(normalizer_1_normalized_fraction),
    .Normalized_Exponent(normalizer_1_normalized_exponent), .Overflow(normalizer_1_overflow),
    .Underflow(normalizer_1_underflow));
  // _7486 7486_1: pin names not known; wires that end beside it: normalizer_1_overflow, normalizer_1_underflow, n7486_1_p3, normalizer_1_underflow, Underflow
  Rounder Rounder (.Normalized_Input(normalizer_1_normalized_fraction), .Output(Rounder_output));
  Normalizer normalizer_2 (
    .Fraction(Rounder_output), .Exponent(normalizer_1_normalized_exponent),
    .Normalized_Fraction(normalizer_2_normalized_fraction), .Normalized_Exponent(Output[30:20]),
    .Overflow(normalizer_2_overflow), .Underflow(normalizer_2_underflow));
  // _74157 74157_1: pin names not known; wires that end beside it: n7486_1_p3, normalizer_2_overflow, normalizer_1_overflow, Overflow, normalizer_2_underflow, 1'b0
  Shifter #(.width(32)) shifter_2 (
    .in(normalizer_2_normalized_fraction), .\dist (5'b00010), .out({Output[19:0], shifter_2_out}));
endmodule

module main (
);

  FPA fpa_1 ();  // open: Input_2, Input_1, Denormalized_Input_1, Denormalized_Input_2, NaN_Input_1, NaN_Input_2, Overflow, Underflow, Output
endmodule
