// Logisim project Multiplexer.circ as structural Verilog: 4 circuits, main circuit main
module main (
);

  MUX_11_bit mux_11_bit_1 ();  // open: X, Y, selection, Output
  MUX_12_bit mux_12_bit_1 ();  // open: X, Y, Selection, Output
  MUX_32_bit mux_32_bit_1 ();  // open: X, Y, Selection, Output
endmodule

// MUX_12
module MUX_12_bit (
  input  [11:0] X,
  input  [11:0] Y,
  input  Selection,
  output [11:0] Output
);

  // _74157 74157_1: pin names not known; wires that end beside it: Selection, X[0], Y[0], Output[0], X[1], Y[1], Output[1], 1'b0, X[2], Y[2], Output[2], X[3], Y[3], Output[3]
  // _74157 74157_2: pin names not known; wires that end beside it: Selection, X[4], Y[4], Output[4], X[5], Y[5], Output[5], 1'b0, X[7], Y[7], Output[7], X[6], Y[6], Output[6]
  // _74157 74157_3: pin names not known; wires that end beside it: Selection, X[8], Y[8], Output[8], X[9], Y[9], Output[9], 1'b0, X[11], Y[11], Output[11], X[10], Y[10], Output[10]
endmodule

// MUX_11
module MUX_11_bit (
  input  [10:0] X,
  input  [10:0] Y,
  input  selection,
  output [10:0] Output
);

  // _74157 74157_1: pin names not known; wires that end beside it: selection, X[0], Y[0], Output[0], X[1], Y[1], Output[1], 1'b0, X[2], Y[2], Output[2], X[3], Y[3], Output[3]
  // _74157 74157_2: pin names not known; wires that end beside it: selection, X[4], Y[4], Output[4], X[5], Y[5], Output[5], 1'b0, X[7], Y[7], Output[7], X[6], Y[6], Output[6]
  // _74157 74157_3: pin names not known; wires that end beside it: selection, X[8], Y[8], Output[8], X[9], Y[9], Output[9], 1'b0, X[10], Y[10], Output[10]
endmodule

// MUX_32
module MUX_32_bit (
  input  [31:0] X,
  input  [31:0] Y,
  input  Selection,
  output [31:0] Output
);

  // _74157 74157_1: pin names not known; wires that end beside it: Selection, X[0], Y[0], Output[0], X[1], Y[1], Output[1], 1'b0, X[2], Y[2], Output[2], X[3], Y[3], Output[3]
  // _74157 74157_2: pin names not known; wires that end beside it: Selection, X[4], Y[4], Output[4], X[5], Y[5], Output[5], 1'b0, X[7], Y[7], Output[7], X[6], Y[6], Output[6]
  // _74157 74157_3: pin names not known; wires that end beside it: Selection, X[8], Y[8], Output[8], X[9], Y[9], Output[9], 1'b0, X[11], Y[11], Output[11], X[10], Y[10], Output[10]
  // _74157 74157_4: pin names not known; wires that end beside it: Selection, X[12], Y[12], Output[12], X[13], Y[13], Output[13], 1'b0, X[15], Y[15], Output[15], X[14], Y[14], Output[14]
  // _74157 74157_5: pin names not known; wires that end beside it: Selection, X[16], Y[16], Output[16], X[17], Y[17], Output[17], 1'b0, X[19], Y[19], Output[19], X[18], Y[18], Output[18]
  // _74157 74157_6: pin names not known; wires that end beside it: Selection, X[20], Y[20], Output[20], X[21], Y[21], Output[21], 1'b0, X[23], Y[23], Output[23], X[22], Y[22], Output[22]
  // _74157 74157_7: pin names not known; wires that end beside it: Selection, X[24], Y[24], Output[24], X[25], Y[25], Output[25], 1'b0, X[27], Y[27], Output[27], X[26], Y[26], Output[26]
  // _74157 74157_8: pin names not known; wires that end beside it: Selection, X[28], Y[28], Output[28], X[29], Y[29], Output[29], 1'b0, X[31], Y[31], Output[31], X[30], Y[30], Output[30]
endmodule
