// Logisim project Rounder.circ as structural Verilog: 2 circuits, main circuit Rounder
module Rounder (
  input  [31:0] Normalized_Input,
  output [31:0] Output
);

  wire n7408_1_p1, n7432_1_p3, n7432_1_p6, n7432_1_p10, n7432_1_p11, n7432_2_p3, n7432_2_p6, n7432_2_p10,
       n7432_2_p11, n7432_2_p16, n7432_3_p1, n7432_3_p3;
  wire [0:0] n7408_1_p5;
  wire [31:20] n7432_2_p15;

  // _7432 7432_1: pin names not known; wires that end beside it: Normalized_Input[7], Normalized_Input[8], n7432_1_p3, n7432_1_p3, Normalized_Input[9], n7432_1_p6, 1'b0, 1'b1, Normalized_Input[6], n7432_1_p10, n7432_1_p11, Normalized_Input[5], n7432_1_p6, n7432_1_p10
  // _7432 7432_2: pin names not known; wires that end beside it: Normalized_Input[2], Normalized_Input[3], n7432_2_p3, n7432_2_p3, Normalized_Input[4], n7432_2_p6, 1'b0, 1'b1, Normalized_Input[1], n7432_2_p10, n7432_2_p11, Normalized_Input[0], n7432_2_p6, n7432_2_p10, n7432_2_p15[20], n7432_2_p16, n7432_2_p16
  // _7432 7432_3: pin names not known; wires that end beside it: n7432_3_p1, Normalized_Input[10], n7432_3_p3, n7432_3_p3, Normalized_Input[12], 1'b1, n7432_1_p11, n7432_2_p11, n7432_3_p1
  // _7408 7408_1: pin names not known; wires that end beside it: n7408_1_p1, 1'b0, n7408_1_p1, Normalized_Input[11], n7408_1_p5[0], 1'b0, 1'b1
  ALU_32_bit _32_bit_ALU (
    .Input_1({{12{1'b0}}, Normalized_Input[31:12]}), .Input_2({{31{1'b0}}, n7408_1_p5[0]}), .Control(2'b10),
    .Output({n7432_2_p15, Output[31:12]}));  // open: Carry_Out, Zero_Flag, Sign_Flag

  assign Output[11:0] = {12{1'b0}};
endmodule

module main (
);

  Rounder rounder_1 ();  // open: Normalized_Input, Output
endmodule
