// Logisim project AddSub.circ as structural Verilog: 2 circuits, main circuit AddSub
module AddSub (
  input  [31:0] X,
  input  [31:0] Y,
  input  SignBit1,
  input  SignBit2,
  output SignOfResult,
  output [31:0] Result
);

  wire [1:1] n7486_1_p3;

  SignDetect signdetect_1 (.X(X), .Y(Y), .SignBit(SignOfResult));
  ALU_32_bit alu_32_bit_1 (
    .Input_1(X), .Input_2(Y), .Control({n7486_1_p3[1], 1'b1}), .Output(Result));  // open: Carry_Out, Zero_Flag, Sign_Flag
  // _7486 7486_1: pin names not known; wires that end beside it: SignBit1, SignBit2, n7486_1_p3[1], 1'b0, 1'b1
endmodule

module SignDetect (
  input  [31:0] X,
  input  [31:0] Y,
  output SignBit
);

  ALU_32_bit alu_32_bit_1 (
    .Input_1(X), .Input_2(Y), .Control(2'b11), .Sign_Flag(SignBit));  // open: Output, Carry_Out, Zero_Flag
endmodule
