// Logisim project MUX_12bit.circ as structural Verilog: 1 circuit, main circuit main
module main (
  input  [11:0] X,
  input  [11:0] Y,
  input  Selection,
  output [11:0] Output
);

  // _74157 74157_1: pin names not known; wires that end beside it: Selection, X[0], Y[0], Output[0], X[1], Y[1], Output[1], 1'b0, X[2], Y[2], Output[2], X[3], Y[3], Output[3]
  // _74157 74157_2: pin names not known; wires that end beside it: Selection, X[4], Y[4], Output[4], X[5], Y[5], Output[5], 1'b0, X[7], Y[7], Output[7], X[6], Y[6], Output[6]
  // _74157 74157_3: pin names not known; wires that end beside it: Selection, X[8], Y[8], Output[8], X[9], Y[9], Output[9], 1'b0, X[11], Y[11], Output[11], X[10], Y[10], Output[10]
endmodule
