// Logisim project Normalizer.circ as structural Verilog: 2 circuits, main circuit main
module main (
  input  [31:0] Fraction,
  input  [11:0] Exponent,
  output [31:0] Normalized_Fraction
);

  wire comparator_11_bit_1_x_y, priority_encoder_32x5_1_valid_bit;
  wire [4:0] comparator_11_bit_1_difference, priority_encoder_32x5_1_a0;
  wire [10:0] mux_11_bit_1_output;
  wire [31:0] shifter_1_out, shifter_2_out;

  MUX_11_bit mux_11_bit_1 (
    .X({11{1'b0}}), .Y(11'h1e), .selection(priority_encoder_32x5_1_valid_bit), .Output(mux_11_bit_1_output));
  Comparator_11_bit comparator_11_bit_1 (
    .X(mux_11_bit_1_output), .Y({{6{1'b0}}, priority_encoder_32x5_1_a0}), .X_Y(comparator_11_bit_1_x_y),
    .DIFFERENCE(comparator_11_bit_1_difference));  // open: SMALLER, LARGER
  Priority_Encoder_32x5 priority_encoder_32x5_1 (
    .in_1(Fraction), .Valid_Bit(priority_encoder_32x5_1_valid_bit), .A4(priority_encoder_32x5_1_a0[4]),
    .A3(priority_encoder_32x5_1_a0[3]), .A2(priority_encoder_32x5_1_a0[2]),
    .A1(priority_encoder_32x5_1_a0[1]), .A0(priority_encoder_32x5_1_a0[0]));
  Shifter #(.width(32)) shifter_1 (.in(Fraction), .\dist (comparator_11_bit_1_difference), .out(shifter_1_out));
  Shifter #(.width(32), .shift("lr")) shifter_2 (
    .in(Fraction), .\dist (comparator_11_bit_1_difference), .out(shifter_2_out));
  MUX_32_bit mux_32_bit_1 (
    ._0(shifter_1_out), ._1(shifter_2_out), .Selection(comparator_11_bit_1_x_y), .Output(Normalized_Fraction));
endmodule

module Normalizer (
  input  [31:0] Fraction,
  input  [11:0] Exponent,
  output [31:0] Normalized_Fraction
);

  wire comparator_11_bit_1_x_y, priority_encoder_32x5_1_valid_bit;
  wire [4:0] comparator_11_bit_1_difference, priority_encoder_32x5_1_a0;
  wire [10:0] mux_11_bit_1_output;
  wire [31:0] shifter_1_out, shifter_2_out;

  MUX_11_bit mux_11_bit_1 (
    .X({11{1'b0}}), .Y(11'h1e), .selection(priority_encoder_32x5_1_valid_bit), .Output(mux_11_bit_1_output));
  Comparator_11_bit comparator_11_bit_1 (
    .X(mux_11_bit_1_output), .Y({{6{1'b0}}, priority_encoder_32x5_1_a0}), .X_Y(comparator_11_bit_1_x_y),
    .DIFFERENCE(comparator_11_bit_1_difference));  // open: SMALLER, LARGER
  Priority_Encoder_32x5 priority_encoder_32x5_1 (
    .in_1(Fraction), .Valid_Bit(priority_encoder_32x5_1_valid_bit), .A4(priority_encoder_32x5_1_a0[4]),
    .A3(priority_encoder_32x5_1_a0[3]), .A2(priority_encoder_32x5_1_a0[2]),
    .A1(priority_encoder_32x5_1_a0[1]), .A0(priority_encoder_32x5_1_a0[0]));
  Shifter #(.width(32)) shifter_1 (.in(Fraction), .\dist (comparator_11_bit_1_difference), .out(shifter_1_out));
  Shifter #(.width(32), .shift("lr")) shifter_2 (
    .in(Fraction), .\dist (comparator_11_bit_1_difference), .out(shifter_2_out));
  MUX_32_bit mux_32_bit_1 (
    ._0(shifter_1_out), ._1(shifter_2_out), .Selection(comparator_11_bit_1_x_y), .Output(Normalized_Fraction));
endmodule
