// Logisim project Normalizer.circ as structural Verilog: 2 circuits, main circuit main
module main (
  input  [31:0] Fraction,
  input  [11:0] Exponent,
  output [31:0] Normalized_Fraction
);

  wire comparator_11_bit_1_x_y, priority_encoder_32x5_1_valid_bit;
  wire [4:0] comparator_11_bit_1_difference, priority_encoder_32x5_1_a0;
  wire [10:0] mux_11_bit_1_output;
  wire [31:0] shifter_1_out, shifter_2_out;

  MUX_11_bit mux_11_bit_1 (
    .X({11{1'b0}}), .Y(11'h1e), .selection(priority_encoder_32x5_1_valid_bit), .Output(mux_11_bit_1_output));
  Comparator_11_bit comparator_11_bit_1 (
    .X(mux_11_bit_1_output), .Y({{6{1'b0}}, priority_encoder_32x5_1_a0}), .X_Y(comparator_11_bit_1_x_y),
    .DIFFERENCE(comparator_11_bit_1_difference));  // open: SMALLER, LARGER
  Priority_Encoder_32x5 priority_encoder_32x5_1 (
    .in_1(Fraction), .Valid_Bit(priority_encoder_32x5_1_valid_bit), .A4(priority_encoder_32x5_1_a0[4]),
    .A3(priority_encoder_32x5_1_a0[3]), .A2(priority_encoder_32x5_1_a0[2]),
    .A1(priority_encoder_32x5_1_a0[1]), .A0(priority_encoder_32x5_1_a0[0]));
  Shifter #(.width(32)) shifter_1 (.in(Fraction), .\dist (comparator_11_bit_1_difference), .out(shifter_1_out));
  Shifter #(.width(32), .shift("lr")) shifter_2 (
    .in(Fraction), .\dist (comparator_11_bit_1_difference), .out(shifter_2_out));
  MUX_32_bit mux_32_bit_1 (
    ._0(shifter_1_out), ._1(shifter_2_out), .Selection(comparator_11_bit_1_x_y), .Output(Normalized_Fraction));
endmodule

module Normalizer (
  input  [31:0] Fraction,
  input  [10:0] Exponent,
  output [31:0] Normalized_Fraction,
  output [10:0] Normalized_Exponent,
  output Overflow,
  output Underflow
);

  wire alu_12_bit_1_sign_flag, alu_12_bit_1_zero_flag, n7408_1_p3, priority_encoder_32x5_1_valid_bit;
  wire [0:0] comparator_11_bit_1_x_y;
  wire [4:0] comparator_11_bit_1_difference, priority_encoder_32x5_1_a0;
  wire [10:0] mux_11_bit_1_output;
  wire [11:0] alu_12_bit_1_output;
  wire [31:0] shifter_1_out, shifter_2_out;

  MUX_11_bit mux_11_bit_1 (
    .X({11{1'b0}}), .Y(11'h1e), .selection(priority_encoder_32x5_1_valid_bit), .Output(mux_11_bit_1_output));
  Comparator_11_bit comparator_11_bit_1 (
    .X(mux_11_bit_1_output), .Y({{6{1'b0}}, priority_encoder_32x5_1_a0}), .X_Y(comparator_11_bit_1_x_y[0]),
    .DIFFERENCE(comparator_11_bit_1_difference));  // open: SMALLER, LARGER
  Priority_Encoder_32x5 priority_encoder_32x5_1 (
    .in_1(Fraction), .Valid_Bit(priority_encoder_32x5_1_valid_bit), .A4(priority_encoder_32x5_1_a0[4]),
    .A3(priority_encoder_32x5_1_a0[3]), .A2(priority_encoder_32x5_1_a0[2]),
    .A1(priority_encoder_32x5_1_a0[1]), .A0(priority_encoder_32x5_1_a0[0]));
  Shifter #(.width(32)) shifter_1 (.in(Fraction), .\dist (comparator_11_bit_1_difference), .out(shifter_1_out));
  Shifter #(.width(32), .shift("lr")) shifter_2 (
    .in(Fraction), .\dist (comparator_11_bit_1_difference), .out(shifter_2_out));
  ALU_12_bit alu_12_bit_1 (
    .Input_1({1'b0, Exponent}), .Input_2({{7{1'b0}}, comparator_11_bit_1_difference}),
    .Control({1'b1, comparator_11_bit_1_x_y[0]}), .Output(alu_12_bit_1_output),
    .Zero_Flag(alu_12_bit_1_zero_flag), .Sign_Flag(alu_12_bit_1_sign_flag));  // open: Carry_Out
  MUX_32_bit mux_32_bit_1 (
    ._0(shifter_1_out), ._1(shifter_2_out), .Selection(comparator_11_bit_1_x_y[0]),
    .Output(Normalized_Fraction));
  // _7408 7408_1: pin names not known; wires that end beside it: alu_12_bit_1_zero_flag, priority_encoder_32x5_1_valid_bit, n7408_1_p3
  // _7432 7432_1: pin names not known; wires that end beside it: alu_12_bit_1_sign_flag, n7408_1_p3, Underflow
  MUX_11_bit mux_11_bit_2 (
    .X({11{1'b0}}), .Y(alu_12_bit_1_output[10:0]), .selection(priority_encoder_32x5_1_valid_bit),
    .Output(Normalized_Exponent));
  ALU_12_bit alu_12_bit_2 (
    .Input_1(12'h7fe), .Input_2(alu_12_bit_1_output), .Control(2'b11), .Sign_Flag(Overflow));  // open: Output, Carry_Out, Zero_Flag
endmodule
