// Logisim project Encoder.circ as structural Verilog: 7 circuits, main circuit main
module main (
  input  [7:0] in_1,
  output out_2,
  output out_3,
  output out_4,
  output out_5
);

  wire IC_74148_Corrected__6__a1, IC_74148_Corrected__7__a2, IC_74148_Corrected__9__a0,
       IC_74148_Corrected__15__neo;

  _74148_Corrected IC_74148_Corrected (
    ._1__I4(in_1[4]), ._2__I5(in_1[5]), ._3__I6(in_1[6]), ._4__I7(in_1[7]),
    ._6__A1(IC_74148_Corrected__6__a1), ._7__A2(IC_74148_Corrected__7__a2), ._8__GND(1'b0), ._16__Vcc(1'b1),
    ._15__nEO(IC_74148_Corrected__15__neo), ._13__I3(in_1[3]), ._12__I2(in_1[2]), ._11__I1(in_1[1]),
    ._10__I0(in_1[0]), ._9__A0(IC_74148_Corrected__9__a0));  // open: _5__nEI__NC, _14__nGS__NC
  // _74157 74157_1: pin names not known; wires that end beside it: IC_74148_Corrected__15__neo, IC_74148_Corrected__9__a0, 1'b0, out_5, IC_74148_Corrected__6__a1, 1'b0, out_4, 1'b0, 1'b1, 1'b0, 1'b1, 1'b0, out_2, IC_74148_Corrected__7__a2, 1'b0, out_3
endmodule

module _74148_Corrected (
  input  _1__I4,
  input  _16__Vcc,
  input  _2__I5,
  input  _3__I6,
  input  _4__I7,
  input  _13__I3,
  input  _5__nEI__NC,
  input  _12__I2,
  input  _11__I1,
  input  _10__I0,
  input  _8__GND,
  output _15__nEO,
  output _14__nGS__NC,
  output _6__A1,
  output _7__A2,
  output _9__A0
);

  Priority_Encoder priority_encoder_1 (
    .in0(_10__I0), .in1(_11__I1), .in2(_12__I2), .in3(_13__I3), .in4(_1__I4), .in5(_2__I5), .in6(_3__I6),
    .in7(_4__I7), .out({_7__A2, _6__A1, _9__A0}), .en_out(_15__nEO));  // open: en_in, gs

  // Notes on the sheet:
  //   74148: 9-Line to 4-Line Priority Encoder
  //   NOTE: Pins 5, 14, and 15 have connections normally, but I chose not to model them
endmodule

// PE_8
module Priority_Encoder_8x3 (
  input  [7:0] in_1,
  output Valid_Bit,
  output A2,
  output A1,
  output A0
);

  wire IC_74148_Corrected__6__a1, IC_74148_Corrected__7__a2, IC_74148_Corrected__9__a0,
       IC_74148_Corrected__15__neo;

  _74148_Corrected IC_74148_Corrected (
    ._1__I4(in_1[4]), ._2__I5(in_1[5]), ._3__I6(in_1[6]), ._4__I7(in_1[7]),
    ._6__A1(IC_74148_Corrected__6__a1), ._7__A2(IC_74148_Corrected__7__a2), ._8__GND(1'b0), ._16__Vcc(1'b1),
    ._15__nEO(IC_74148_Corrected__15__neo), ._13__I3(in_1[3]), ._12__I2(in_1[2]), ._11__I1(in_1[1]),
    ._10__I0(in_1[0]), ._9__A0(IC_74148_Corrected__9__a0));  // open: _5__nEI__NC, _14__nGS__NC
  // _74157 74157_1: pin names not known; wires that end beside it: IC_74148_Corrected__15__neo, IC_74148_Corrected__9__a0, 1'b0, A0, IC_74148_Corrected__6__a1, 1'b0, A1, 1'b0, 1'b1, 1'b0, 1'b1, 1'b0, Valid_Bit, IC_74148_Corrected__7__a2, 1'b0, A2
endmodule

// PE_16
module Priority_Encoder_16x4 (
  input  [15:0] in_1,
  output Valid_Bit,
  output A3,
  output A2,
  output A1,
  output A0
);

  wire priority_encoder_8x3_1_a0, priority_encoder_8x3_1_a1, priority_encoder_8x3_1_a2,
       priority_encoder_8x3_1_valid_bit, priority_encoder_8x3_2_a0, priority_encoder_8x3_2_a1,
       priority_encoder_8x3_2_a2;

  Priority_Encoder_8x3 priority_encoder_8x3_1 (
    .in_1(in_1[7:0]), .Valid_Bit(priority_encoder_8x3_1_valid_bit), .A2(priority_encoder_8x3_1_a2),
    .A1(priority_encoder_8x3_1_a1), .A0(priority_encoder_8x3_1_a0));
  Priority_Encoder_8x3 priority_encoder_8x3_2 (
    .in_1(in_1[15:8]), .Valid_Bit(A3), .A2(priority_encoder_8x3_2_a2), .A1(priority_encoder_8x3_2_a1),
    .A0(priority_encoder_8x3_2_a0));
  // _74157 74157_1: pin names not known; wires that end beside it: A3, priority_encoder_8x3_1_a0, priority_encoder_8x3_2_a0, A0, priority_encoder_8x3_1_a1, priority_encoder_8x3_2_a1, A1, 1'b0, 1'b1, 1'b0, priority_encoder_8x3_1_valid_bit, 1'b1, Valid_Bit, priority_encoder_8x3_1_a2, priority_encoder_8x3_2_a2, A2
endmodule

module Priority_Encoder_32x5 (
  input  [31:0] in_1,
  output Valid_Bit,
  output A4,
  output A3,
  output A2,
  output A1,
  output A0
);

  wire priority_encoder_16x4_1_a0, priority_encoder_16x4_1_a1, priority_encoder_16x4_1_a2,
       priority_encoder_16x4_1_a3, priority_encoder_16x4_1_valid_bit, priority_encoder_16x4_2_a0,
       priority_encoder_16x4_2_a1, priority_encoder_16x4_2_a2, priority_encoder_16x4_2_a3;

  Priority_Encoder_16x4 priority_encoder_16x4_1 (
    .in_1(in_1[15:0]), .Valid_Bit(priority_encoder_16x4_1_valid_bit), .A3(priority_encoder_16x4_1_a3),
    .A2(priority_encoder_16x4_1_a2), .A1(priority_encoder_16x4_1_a1), .A0(priority_encoder_16x4_1_a0));
  Priority_Encoder_16x4 priority_encoder_16x4_2 (
    .in_1(in_1[31:16]), .Valid_Bit(A4), .A3(priority_encoder_16x4_2_a3), .A2(priority_encoder_16x4_2_a2),
    .A1(priority_encoder_16x4_2_a1), .A0(priority_encoder_16x4_2_a0));
  // _74157 74157_1: pin names not known; wires that end beside it: A4, priority_encoder_16x4_1_a3, priority_encoder_16x4_2_a3, A3, 1'b0, 1'b1, 1'b0
  // _74157 74157_2: pin names not known; wires that end beside it: A4, priority_encoder_16x4_1_a0, priority_encoder_16x4_2_a0, A0, priority_encoder_16x4_1_a1, priority_encoder_16x4_2_a1, A1, 1'b0, 1'b1, 1'b0, priority_encoder_16x4_1_valid_bit, 1'b1, Valid_Bit, priority_encoder_16x4_1_a2, priority_encoder_16x4_2_a2, A2
endmodule

module Priority_Encoder_12x4 (
  input  [11:0] in_1,
  output Valid_Bit,
  output A3,
  output A2,
  output A1,
  output A0
);

  wire priority_encoder_8x3_1_a0, priority_encoder_8x3_1_a1, priority_encoder_8x3_1_a2,
       priority_encoder_8x3_1_valid_bit, priority_encoder_8x3_2_a0, priority_encoder_8x3_2_a1,
       priority_encoder_8x3_2_a2;

  Priority_Encoder_8x3 priority_encoder_8x3_1 (
    .in_1(in_1[7:0]), .Valid_Bit(priority_encoder_8x3_1_valid_bit), .A2(priority_encoder_8x3_1_a2),
    .A1(priority_encoder_8x3_1_a1), .A0(priority_encoder_8x3_1_a0));
  Priority_Encoder_8x3 priority_encoder_8x3_2 (
    .in_1({4'b0000, in_1[11:8]}), .Valid_Bit(A3), .A2(priority_encoder_8x3_2_a2),
    .A1(priority_encoder_8x3_2_a1), .A0(priority_encoder_8x3_2_a0));
  // _74157 74157_1: pin names not known; wires that end beside it: A3, priority_encoder_8x3_1_a0, priority_encoder_8x3_2_a0, A0, priority_encoder_8x3_1_a1, priority_encoder_8x3_2_a1, A1, 1'b0, 1'b1, 1'b0, priority_encoder_8x3_1_valid_bit, 1'b1, Valid_Bit, priority_encoder_8x3_1_a2, priority_encoder_8x3_2_a2, A2
endmodule

module Priority_Encoder_10x4 (
  input  [9:0] in_1,
  output Valid_Bit,
  output A3,
  output A2,
  output A1,
  output A0
);

  wire priority_encoder_8x3_1_a0, priority_encoder_8x3_1_a1, priority_encoder_8x3_1_a2,
       priority_encoder_8x3_1_valid_bit, priority_encoder_8x3_2_a0, priority_encoder_8x3_2_a1,
       priority_encoder_8x3_2_a2;

  Priority_Encoder_8x3 priority_encoder_8x3_1 (
    .in_1(in_1[7:0]), .Valid_Bit(priority_encoder_8x3_1_valid_bit), .A2(priority_encoder_8x3_1_a2),
    .A1(priority_encoder_8x3_1_a1), .A0(priority_encoder_8x3_1_a0));
  Priority_Encoder_8x3 priority_encoder_8x3_2 (
    .in_1({{6{1'b0}}, in_1[9:8]}), .Valid_Bit(A3), .A2(priority_encoder_8x3_2_a2),
    .A1(priority_encoder_8x3_2_a1), .A0(priority_encoder_8x3_2_a0));
  // _74157 74157_1: pin names not known; wires that end beside it: A3, priority_encoder_8x3_1_a0, priority_encoder_8x3_2_a0, A0, priority_encoder_8x3_1_a1, priority_encoder_8x3_2_a1, A1, 1'b0, 1'b1, 1'b0, priority_encoder_8x3_1_valid_bit, 1'b1, Valid_Bit, priority_encoder_8x3_1_a2, priority_encoder_8x3_2_a2, A2
endmodule
