// Logisim project Floating_Point_Adder.circ as structural Verilog: 1 circuit, main circuit main
// smaller
module main (
  input  [31:0] in_1,
  input  [31:0] in_2,
  output sign_inp2,
  output Sign_inp1,
  output sign_result,
  output [31:0] result,
  output [10:0] out_7
);

  wire [4:0] Comparator_difference;
  wire [31:0] Comparator_largerfraction, Comparator_smallerfraction, shifter_1_out;

  Comparator_With_Smaller_Fraction Comparator (
    .X_fraction({2'b01, in_2[19:0], {10{1'b0}}}), .Y_fraction({2'b01, in_1[19:0], {10{1'b0}}}),
    .X(in_2[30:20]), .Y(in_1[30:20]), .LargerFraction(Comparator_largerfraction),
    .SmallerFraction(Comparator_smallerfraction), .Common_Exponent(out_7), .Difference(Comparator_difference));  // open: X_Y
  Shifter #(.width(32), .shift("lr")) shifter_1 (
    .in(Comparator_smallerfraction), .\dist (Comparator_difference), .out(shifter_1_out));
  AddSub addsub_1 (
    .X(Comparator_largerfraction), .Y(shifter_1_out), .SignBit1(in_2[31]), .SignBit2(in_1[31]),
    .SignOfResult(sign_result), .Result(result));

  assign Sign_inp1 = in_2[31];
  assign sign_inp2 = in_1[31];
endmodule
