// Logisim project Multiplexer.circ as structural Verilog: 4 circuits, main circuit main
module main (
);

  MUX_11_bit mux_11_bit_1 ();  // open: X, Y, selection, Output
  MUX_12_bit mux_12_bit_1 ();  // open: X, Y, Selection, Output
  MUX_32_bit mux_32_bit_1 ();  // open: _0, _1, Selection, Output
endmodule

// MUX_12
module MUX_12_bit (
  input  [11:0] X,
  input  [11:0] Y,
  input  Selection,
  output [11:0] Output
);

  // _74157 74157_1: pin names not known; wires that end beside it: Selection, X[0], Y[0], Output[0], X[1], Y[1], Output[1], 1'b0, X[2], Y[2], Output[2], X[3], Y[3], Output[3]
  // _74157 74157_2: pin names not known; wires that end beside it: Selection, X[4], Y[4], Output[4], X[5], Y[5], Output[5], 1'b0, X[7], Y[7], Output[7], X[6], Y[6], Output[6]
  // _74157 74157_3: pin names not known; wires that end beside it: Selection, X[8], Y[8], Output[8], X[9], Y[9], Output[9], 1'b0, X[11], Y[11], Output[11], X[10], Y[10], Output[10]
endmodule

// MUX_11
module MUX_11_bit (
  input  [10:0] X,
  input  [10:0] Y,
  input  selection,
  output [10:0] Output
);

  // _74157 74157_1: pin names not known; wires that end beside it: selection, X[0], Y[0], Output[0], X[1], Y[1], Output[1], 1'b0, X[2], Y[2], Output[2], X[3], Y[3], Output[3]
  // _74157 74157_2: pin names not known; wires that end beside it: selection, X[4], Y[4], Output[4], X[5], Y[5], Output[5], 1'b0, X[7], Y[7], Output[7], X[6], Y[6], Output[6]
  // _74157 74157_3: pin names not known; wires that end beside it: selection, X[8], Y[8], Output[8], X[9], Y[9], Output[9], 1'b0, X[10], Y[10], Output[10]
endmodule

// MUX_32
module MUX_32_bit (
  input  [31:0] _0,
  input  [31:0] _1,
  input  Selection,
  output [31:0] Output
);

  // _74157 74157_1: pin names not known; wires that end beside it: Selection, _0[0], _1[0], Output[0], _0[1], _1[1], Output[1], 1'b0, _0[2], _1[2], Output[2], _0[3], _1[3], Output[3]
  // _74157 74157_2: pin names not known; wires that end beside it: Selection, _0[4], _1[4], Output[4], _0[5], _1[5], Output[5], 1'b0, _0[7], _1[7], Output[7], _0[6], _1[6], Output[6]
  // _74157 74157_3: pin names not known; wires that end beside it: Selection, _0[8], _1[8], Output[8], _0[9], _1[9], Output[9], 1'b0, _0[11], _1[11], Output[11], _0[10], _1[10], Output[10]
  // _74157 74157_4: pin names not known; wires that end beside it: Selection, _0[12], _1[12], Output[12], _0[13], _1[13], Output[13], 1'b0, _0[15], _1[15], Output[15], _0[14], _1[14], Output[14]
  // _74157 74157_5: pin names not known; wires that end beside it: Selection, _0[16], _1[16], Output[16], _0[17], _1[17], Output[17], 1'b0, _0[19], _1[19], Output[19], _0[18], _1[18], Output[18]
  // _74157 74157_6: pin names not known; wires that end beside it: Selection, _0[20], _1[20], Output[20], _0[21], _1[21], Output[21], 1'b0, _0[23], _1[23], Output[23], _0[22], _1[22], Output[22]
  // _74157 74157_7: pin names not known; wires that end beside it: Selection, _0[24], _1[24], Output[24], _0[25], _1[25], Output[25], 1'b0, _0[27], _1[27], Output[27], _0[26], _1[26], Output[26]
  // _74157 74157_8: pin names not known; wires that end beside it: Selection, _0[28], _1[28], Output[28], _0[29], _1[29], Output[29], 1'b0, _0[31], _1[31], Output[31], _0[30], _1[30], Output[30]
endmodule
