// Logisim project AddSub.circ as structural Verilog: 1 circuit, main circuit AddSub
module AddSub (
  input  [31:0] X,
  input  [31:0] Y,
  input  SignBit1,
  input  SignBit2,
  output Sign_of_Result,
  output [31:0] Result
);

  wire alu_32_bit_1_sign_flag, alu_32_bit_1_zero_flag, n7404_1_p2, n7404_1_p4, n7408_1_p3, n7408_1_p6,
       n7408_1_p9, n7408_1_p10;
  wire [0:0] n7408_1_p8;
  wire [31:0] alu_32_bit_1_output, alu_32_bit_2_output;

  ALU_32_bit alu_32_bit_1 (
    .Input_1(X), .Input_2(Y), .Control({1'b1, n7408_1_p8[0]}), .Output(alu_32_bit_1_output),
    .Zero_Flag(alu_32_bit_1_zero_flag), .Sign_Flag(alu_32_bit_1_sign_flag));  // open: Carry_Out
  // _7404 7404_1: pin names not known; wires that end beside it: alu_32_bit_1_sign_flag, n7404_1_p2, alu_32_bit_1_zero_flag, n7404_1_p4
  // _7408 7408_1: pin names not known; wires that end beside it: n7404_1_p2, SignBit1, n7408_1_p3, alu_32_bit_1_sign_flag, SignBit2, n7408_1_p6, alu_32_bit_1_sign_flag, n7408_1_p8[0], n7408_1_p9, n7408_1_p10, n7404_1_p4, Sign_of_Result
  ALU_32_bit alu_32_bit_2 (
    .Input_1(alu_32_bit_1_output), .Input_2({32{1'b0}}), .Control(2'b01), .Output(alu_32_bit_2_output));  // open: Carry_Out, Zero_Flag, Sign_Flag
  // _7486 7486_1: pin names not known; wires that end beside it: SignBit1, SignBit2, n7408_1_p8[0], 1'b1
  // _7432 7432_1: pin names not known; wires that end beside it: n7408_1_p3, n7408_1_p6, n7408_1_p10
  MUX_32_bit mux_32_bit_1 (._0(alu_32_bit_1_output), ._1(alu_32_bit_2_output), .Selection(n7408_1_p9), .Output(Result));
endmodule
