// Logisim project ALU.circ as structural Verilog: 5 circuits, main circuit main
module main (
);

  ALU_8_bit alu_8_bit_1 ();  // open: Input_1, Input_2, Control, Output, Carry_Out, Zero_Flag, Sign_Flag
  ALU_12_bit alu_12_bit_1 ();  // open: Input_1, Input_2, Control, Output, Carry_Out, Zero_Flag, Sign_Flag
  ALU_16_bit alu_16_bit_1 ();  // open: Input_1, Input_2, Control, Output, Carry_Out, Zero_Flag, Sign_Flag
  ALU_32_bit alu_32_bit_1 ();  // open: Input_1, Input_2, Control, Output, Carry_Out, Zero_Flag, Sign_Flag
endmodule

// ALU_12
module ALU_12_bit (
  input  [11:0] Input_1,
  input  [11:0] Input_2,
  input  [1:0] Control,
  output [11:0] Output,
  output Carry_Out,
  output Zero_Flag,
  output Sign_Flag
);

  wire adder_1_cout, bitfinder_1_found, subtractor_1_bout, subtractor_2_bout;
  wire [11:0] adder_1_out, negator_1_out, subtractor_1_out, subtractor_2_out;

  Subtractor #(.width(12)) subtractor_1 (
    .a(Input_1), .b(12'h1), .out(subtractor_1_out), .bin(1'b0), .bout(subtractor_1_bout));
  Negator #(.width(12)) negator_1 (.in(Input_1), .out(negator_1_out));
  Adder #(.width(12)) adder_1 (.a(Input_1), .b(Input_2), .out(adder_1_out), .cin(1'b0), .cout(adder_1_cout));
  Subtractor #(.width(12)) subtractor_2 (
    .a(Input_1), .b(Input_2), .out(subtractor_2_out), .bin(1'b0), .bout(subtractor_2_bout));
  Multiplexer #(.select(2), .width(12)) multiplexer_1 (
    .in0(subtractor_1_out), .in1(negator_1_out), .in2(adder_1_out), .in3(subtractor_2_out), .out(Output),
    .sel(Control), .en(1'b1));
  Multiplexer #(.select(2)) multiplexer_2 (
    .in0(subtractor_1_bout), .in1(1'b0), .in2(adder_1_cout), .in3(subtractor_2_bout), .out(Carry_Out),
    .sel(Control), .en(1'b1));
  BitFinder #(.width(12)) bitfinder_1 (.in(Output), .found(bitfinder_1_found));  // open: index
  not not_1 (Zero_Flag, bitfinder_1_found);

  assign Sign_Flag = Output[11];
endmodule

// ALU_32
module ALU_32_bit (
  input  [31:0] Input_1,
  input  [31:0] Input_2,
  input  [1:0] Control,
  output [31:0] Output,
  output Carry_Out,
  output Zero_Flag,
  output Sign_Flag
);

  wire adder_1_cout, bitfinder_1_found, subtractor_1_bout, subtractor_2_bout;
  wire [31:0] adder_1_out, negator_1_out, subtractor_1_out, subtractor_2_out;

  Subtractor #(.width(32)) subtractor_1 (
    .a(Input_1), .b(32'h1), .out(subtractor_1_out), .bin(1'b0), .bout(subtractor_1_bout));
  Negator #(.width(32)) negator_1 (.in(Input_1), .out(negator_1_out));
  Adder #(.width(32)) adder_1 (.a(Input_1), .b(Input_2), .out(adder_1_out), .cin(1'b0), .cout(adder_1_cout));
  Subtractor #(.width(32)) subtractor_2 (
    .a(Input_1), .b(Input_2), .out(subtractor_2_out), .bin(1'b0), .bout(subtractor_2_bout));
  Multiplexer #(.select(2), .width(32)) multiplexer_1 (
    .in0(subtractor_1_out), .in1(negator_1_out), .in2(adder_1_out), .in3(subtractor_2_out), .out(Output),
    .sel(Control), .en(1'b1));
  Multiplexer #(.select(2)) multiplexer_2 (
    .in0(subtractor_1_bout), .in1(1'b0), .in2(adder_1_cout), .in3(subtractor_2_bout), .out(Carry_Out),
    .sel(Control), .en(1'b1));
  BitFinder #(.width(32)) bitfinder_1 (.in(Output), .found(bitfinder_1_found));  // open: index
  not not_1 (Zero_Flag, bitfinder_1_found);

  assign Sign_Flag = Output[31];
endmodule

// ALU_8
module ALU_8_bit (
  input  [7:0] Input_1,
  input  [7:0] Input_2,
  input  [1:0] Control,
  output [7:0] Output,
  output Carry_Out,
  output Zero_Flag,
  output Sign_Flag
);

  wire adder_1_cout, bitfinder_1_found, subtractor_1_bout, subtractor_2_bout;
  wire [7:0] adder_1_out, negator_1_out, subtractor_1_out, subtractor_2_out;

  Subtractor subtractor_1 (.a(Input_1), .b(8'h1), .out(subtractor_1_out), .bin(1'b0), .bout(subtractor_1_bout));
  Negator negator_1 (.in(Input_1), .out(negator_1_out));
  Adder adder_1 (.a(Input_1), .b(Input_2), .out(adder_1_out), .cin(1'b0), .cout(adder_1_cout));
  Subtractor subtractor_2 (.a(Input_1), .b(Input_2), .out(subtractor_2_out), .bin(1'b0), .bout(subtractor_2_bout));
  Multiplexer #(.select(2), .width(8)) multiplexer_1 (
    .in0(subtractor_1_out), .in1(negator_1_out), .in2(adder_1_out), .in3(subtractor_2_out), .out(Output),
    .sel(Control), .en(1'b1));
  Multiplexer #(.select(2)) multiplexer_2 (
    .in0(subtractor_1_bout), .in1(1'b0), .in2(adder_1_cout), .in3(subtractor_2_bout), .out(Carry_Out),
    .sel(Control), .en(1'b1));
  BitFinder bitfinder_1 (.in(Output), .found(bitfinder_1_found));  // open: index
  not not_1 (Zero_Flag, bitfinder_1_found);

  assign Sign_Flag = Output[7];
endmodule

// ALU_16
module ALU_16_bit (
  input  [15:0] Input_1,
  input  [15:0] Input_2,
  input  [1:0] Control,
  output [15:0] Output,
  output Carry_Out,
  output Zero_Flag,
  output Sign_Flag
);

  wire adder_1_cout, bitfinder_1_found, subtractor_1_bout, subtractor_2_bout;
  wire [15:0] adder_1_out, negator_1_out, subtractor_1_out, subtractor_2_out;

  Subtractor #(.width(16)) subtractor_1 (
    .a(Input_1), .b(16'h1), .out(subtractor_1_out), .bin(1'b0), .bout(subtractor_1_bout));
  Negator #(.width(16)) negator_1 (.in(Input_1), .out(negator_1_out));
  Adder #(.width(16)) adder_1 (.a(Input_1), .b(Input_2), .out(adder_1_out), .cin(1'b0), .cout(adder_1_cout));
  Subtractor #(.width(16)) subtractor_2 (
    .a(Input_1), .b(Input_2), .out(subtractor_2_out), .bin(1'b0), .bout(subtractor_2_bout));
  Multiplexer #(.select(2), .width(16)) multiplexer_1 (
    .in0(subtractor_1_out), .in1(negator_1_out), .in2(adder_1_out), .in3(subtractor_2_out), .out(Output),
    .sel(Control), .en(1'b1));
  Multiplexer #(.select(2)) multiplexer_2 (
    .in0(subtractor_1_bout), .in1(1'b0), .in2(adder_1_cout), .in3(subtractor_2_bout), .out(Carry_Out),
    .sel(Control), .en(1'b1));
  BitFinder #(.width(16)) bitfinder_1 (.in(Output), .found(bitfinder_1_found));  // open: index
  not not_1 (Zero_Flag, bitfinder_1_found);

  assign Sign_Flag = Output[15];
endmodule
