// Logisim project Utility.circ as structural Verilog
module Validity_Checker (
  input  [31:0] Fraction,
  input  [10:0] Exponent,
  output Denormalized_Flag,
  output [31:0] Valid_Fraction
);

  wire priority_encoder_32x5_1_p2, priority_encoder_32x5_1_p3, priority_encoder_32x5_1_p4;
  wire [31:0] shifter_1_out;

  Shifter #(.width(32)) shifter_1 (.in(Fraction), .\dist (5'b00010), .out(shifter_1_out));
  // Priority_Encoder_32x5 priority_encoder_32x5_1: pin names not known; wires that end beside it: shifter_1_out, priority_encoder_32x5_1_p2, priority_encoder_32x5_1_p3, priority_encoder_32x5_1_p4
  Priority_Encoder_12x4 priority_encoder_12x4_1 (
    .in_1({1'b0, Exponent}), .Valid_Bit(priority_encoder_32x5_1_p3));  // open: A3, A2, A1, A0
  // ALU_12_bit alu_12_bit_1: pin names not known
  // _7404 7404_1: pin names not known
  // _7408 7408_1: pin names not known; wires that end beside it: priority_encoder_32x5_1_p2, priority_encoder_32x5_1_p4, Denormalized_Flag
  MUX_32_bit mux_32_bit_1 (
    ._0({32{1'b0}}), ._1(Fraction), .Selection(priority_encoder_32x5_1_p3), .Output(Valid_Fraction));
endmodule
