// Logisim project Floating_Point_Adder.circ as structural Verilog: 1 circuit, main circuit main
// smaller
module main (
  input  [31:0] in_1,
  input  [31:0] in_2,
  output Denormalized_Input_1,
  output Denormalized_Input_2,
  output Overflow,
  output Underflow,
  output [31:0] Output
);

  wire n7486_1_p3, normalizer_1_overflow, normalizer_1_underflow, normalizer_2_overflow,
       normalizer_2_underflow;
  wire [4:0] Comparator_difference;
  wire [10:0] Comparator_common_exponent, normalizer_1_normalized_exponent;
  wire [11:0] shifter_2_out;
  wire [31:0] AddSub_result, Comparator_largerfraction, Comparator_smallerfraction,
       normalizer_1_normalized_fraction, normalizer_2_normalized_fraction, Rounder_output, shifter_1_out,
       validity_checker_1_valid_fraction, validity_checker_2_valid_fraction;

  Validity_Checker validity_checker_1 (
    .Fraction({2'b01, in_2[19:0], {10{1'b0}}}), .Exponent(in_2[30:20]),
    .Denormalized_Flag(Denormalized_Input_1), .Valid_Fraction(validity_checker_1_valid_fraction));
  Comparator_With_Smaller_Fraction Comparator (
    .X_fraction(validity_checker_1_valid_fraction), .Y_fraction(validity_checker_2_valid_fraction),
    .X(in_2[30:20]), .Y(in_1[30:20]), .LargerFraction(Comparator_largerfraction),
    .SmallerFraction(Comparator_smallerfraction), .Common_Exponent(Comparator_common_exponent),
    .Difference(Comparator_difference));  // open: X_Y
  Shifter #(.width(32), .shift("lr")) shifter_1 (
    .in(Comparator_smallerfraction), .\dist (Comparator_difference), .out(shifter_1_out));
  AddSub AddSub (
    .X(Comparator_largerfraction), .Y(shifter_1_out), .SignBit1(in_2[31]), .SignBit2(in_1[31]),
    .SignOfResult(Output[31]), .Result(AddSub_result));
  Validity_Checker validity_checker_2 (
    .Fraction({2'b01, in_1[19:0], {10{1'b0}}}), .Exponent(in_1[30:20]),
    .Denormalized_Flag(Denormalized_Input_2), .Valid_Fraction(validity_checker_2_valid_fraction));
  Normalizer normalizer_1 (
    .Fraction(AddSub_result), .Exponent(Comparator_common_exponent),
    .Normalized_Fraction(normalizer_1_normalized_fraction),
    .Normalized_Exponent(normalizer_1_normalized_exponent), .Overflow(normalizer_1_overflow),
    .Underflow(normalizer_1_underflow));
  // _7486 7486_1: pin names not known; wires that end beside it: normalizer_1_overflow, normalizer_1_underflow, n7486_1_p3, normalizer_1_underflow, Underflow
  Rounder_main Rounder (.Normalized_Input(normalizer_1_normalized_fraction), .Output(Rounder_output));
  Normalizer normalizer_2 (
    .Fraction(Rounder_output), .Exponent(normalizer_1_normalized_exponent),
    .Normalized_Fraction(normalizer_2_normalized_fraction), .Normalized_Exponent(Output[30:20]),
    .Overflow(normalizer_2_overflow), .Underflow(normalizer_2_underflow));
  // _74157 74157_1: pin names not known; wires that end beside it: n7486_1_p3, normalizer_2_overflow, normalizer_1_overflow, Overflow, normalizer_2_underflow, 1'b0
  Shifter #(.width(32)) shifter_2 (
    .in(normalizer_2_normalized_fraction), .\dist (5'b00010), .out({Output[19:0], shifter_2_out}));
endmodule
